// Logisim project Assignment0.circ as structural Verilog: 1 circuit, main circuit main
module main (
  input  A,
  input  B,
  output Out
);

  and and_1 (Out, A, B);

  // Notes on the sheet:
  //   Name: Ammon Phipps
  //   Assignment 0 Submission
endmodule
