// Logisim project Assignment1.circ as structural Verilog: 11 circuits, main circuit Not
module Not (
  input  in,
  output out
);

  nand nand_1 (out, in, in);

  // Notes on the sheet:
  //   Use only a built-in Nand gate for this (found in Gates>NAND).
  //   Once you are done go to Simulate>Test Vector.
  //   Select the Not.txt file, and run it to try the test cases
endmodule

module And (
  input  a,
  input  b,
  output out
);

  wire nand_1_out;

  nand nand_1 (nand_1_out, a, b);
  nand nand_2 (out, nand_1_out, nand_1_out);

  // Notes on the sheet:
  //   Simple Gate Implementation using Nand and Not
  //   For all gates in this assignment (except Nand),you are required to use
  //   the custom subcircuits you build, rather than the built-in gates.
  //   NAND Gate 1
  //   NAND Gate 2
endmodule

module Or (
  input  a,
  input  b,
  output out
);

  wire nand_1_out, nand_2_out;

  nand nand_1 (nand_1_out, a, a);
  nand nand_2 (nand_2_out, b, b);
  nand nand_3 (out, nand_1_out, nand_2_out);

  // Notes on the sheet:
  //   This function can be defined in terms of boolean expressions previously implemented
  //   It helps to start by looking at the expression as Not(Not(A Or B)) and using boolean
  //   algebra to transform this into something we can implement
  //   A NAND
  //   B NAND
  //   AB NAND
endmodule

module Xor (
  input  a,
  input  b,
  output out
);

  wire b__1a_out, nand_1_out, nand_2_out, nand_3_out;

  nand nand_1 (nand_1_out, a, a);
  nand nand_2 (nand_2_out, b, b);
  nand nand_3 (nand_3_out, a, nand_2_out);
  nand b__1a (b__1a_out, nand_1_out, b);
  nand _2a__2b (out, nand_3_out, b__1a_out);

  // Notes on the sheet:
  //   This function can also be defined in terms of boolean expressions already created. 
  //   Try to express what the Xor gate does in english, then translate that to a boolean
  //   expression that you can implement!
  //   a,a
  //   NAND 1a
  //   b,b
  //   NAND 1b
  //   a, 1b
  //   nand 2a
  //   NAND 2b
  //   NAND 3
  //   the XOR gate is similar to the OR gate, but its different in that it has to be
  //   one or the other it can't be both A and B
endmodule

module Mux (
  input  sel,
  input  a,
  input  b,
  output out
);

  wire B__sel_out, nand_1_out, sel_sel_out;

  nand B__sel (B__sel_out, sel, b);
  nand nand_1 (nand_1_out, sel_sel_out, a);
  nand sel_sel (sel_sel_out, sel, sel);
  nand t__u (out, nand_1_out, B__sel_out);

  // Notes on the sheet:
  //   Function:
  //   If sel == 0, out = a;
  //   	else out = b;
  //   Can be implemented with And, or and Not. Try a truth table!
  //   NAND u
  //   NAND t
  //   NAND n
  //   NAND v
endmodule

module DMux (
  input  sel,
  input  in,
  output a,
  output b
);

  wire in___t_out, in__s_out, sel_sel_out;

  nand in___t (in___t_out, sel_sel_out, in);
  nand u_u (a, in___t_out, in___t_out);
  nand sel_sel (sel_sel_out, sel, sel);
  nand in__s (in__s_out, sel, in);
  nand v_v (b, in__s_out, in__s_out);

  // Notes on the sheet:
  //   Function:
  //   If sel == 0, [a, b] = [in, 0]
  //   	else, [a, b] = [0, in]
  //   Same as before, use a truth table and basic logic gates.
  //   nand u
  //   nand w
  //   nand t
  //   nand v
  //   nand x
endmodule

module Not16 (
  input  [15:0] in,
  output [15:0] out
);

  nand nand_1 (out[0], in[0], in[0]);
  nand nand_2 (out[1], in[1], in[1]);
  nand nand_3 (out[2], in[2], in[2]);
  nand nand_4 (out[3], in[3], in[3]);
  nand nand_5 (out[4], in[4], in[4]);
  nand nand_6 (out[5], in[5], in[5]);
  nand nand_7 (out[6], in[6], in[6]);
  nand nand_8 (out[7], in[7], in[7]);
  nand nand_9 (out[8], in[8], in[8]);
  nand nand_10 (out[9], in[9], in[9]);
  nand nand_11 (out[10], in[10], in[10]);
  nand nand_12 (out[11], in[11], in[11]);
  nand nand_13 (out[12], in[12], in[12]);
  nand nand_14 (out[13], in[13], in[13]);
  nand nand_15 (out[14], in[14], in[14]);
  nand nand_16 (out[15], in[15], in[15]);

  // Notes on the sheet:
  //   Function:
  //   For all i from 0 .. 15, out[i] = Not(in[i])
  //   These are rather repetitive, you will use the splitter element (shown below)
  //   a lot. You already have an elementary version of each of these gates, the implementation
  //   of a 16-bit gate is just a matter of constructing an array of n elementary gates, where
  //   each gate operates separately on each bit.
  //   Changing the spacing attribute on the splitter can help a lot for these
endmodule

module And16 (
  input  [15:0] a,
  input  [15:0] b,
  output [15:0] out
);

  wire [15:0] nand_1_out;

  assign nand_1_out = ~(a & b);  // NAND_Gate nand_1, 16 bits wide
  Not16 not16_1 (.in(nand_1_out), .out(out));

  // Notes on the sheet:
  //   Function:
  //   For all i from 0 .. 15, out[i] = And(in[i])
  //   Reuse the not16 gate i made
endmodule

module Or16 (
  input  [15:0] a,
  input  [15:0] b,
  output [15:0] out
);

  wire [15:0] not16_1_out, not16_2_out;

  Not16 not16_1 (.in(a), .out(not16_1_out));
  Not16 not16_2 (.in(b), .out(not16_2_out));
  assign out = ~(not16_1_out & not16_2_out);  // NAND_Gate A_B, 16 bits wide

  // Notes on the sheet:
  //   Function:
  //   For all i from 0 .. 15, out[i] = Or(in[i])
  //   not16 A
  //   not16 B
  //   nand C
endmodule

module Mux16 (
  input  sel,
  input  [15:0] a,
  input  [15:0] b,
  output [15:0] out
);

  wire [15:0] and16_1_out, and16_2_out, not16_1_out;

  And16 and16_1 (.a(not16_1_out), .b(a), .out(and16_1_out));
  And16 and16_2 (.a({16{sel}}), .b(b), .out(and16_2_out));
  Not16 not16_1 (.in({16{sel}}), .out(not16_1_out));
  Or16 or16_1 (.a(and16_1_out), .b(and16_2_out), .out(out));

  // Notes on the sheet:
  //   Function:
  //   If sel == 0, out = a
  //   	else, out = b
  //   An n-bit multiplexer is just the result of feeding the same selection bit
  //   into n 1-bit multiplexers. Again, splitters and lots of the elementary version
  //   of the gate.
endmodule

module Or8Way (
  input  [7:0] in,
  output out
);

  wire _1a_1b_out, _1c_1d_out, in_0__in_1_out, in_2__in_3_out, in_4__in_5_out, in_6__in_7_out;

  Or in_0__in_1 (.a(in[0]), .b(in[1]), .out(in_0__in_1_out));
  Or in_2__in_3 (.a(in[2]), .b(in[3]), .out(in_2__in_3_out));
  Or in_4__in_5 (.a(in[4]), .b(in[5]), .out(in_4__in_5_out));
  Or in_6__in_7 (.a(in[6]), .b(in[7]), .out(in_6__in_7_out));
  Or _1a_1b (.a(in_0__in_1_out), .b(in_2__in_3_out), .out(_1a_1b_out));
  Or _1c_1d (.a(in_4__in_5_out), .b(in_6__in_7_out), .out(_1c_1d_out));
  Or _2a_2b (.a(_1a_1b_out), .b(_1c_1d_out), .out(out));

  // Notes on the sheet:
  //   Function:
  //   Out = in[0] Or in[1] Or ... Or in[7]
  //   Think forks for this one
  //   Try to get a 3-way Or gate first, then use the same process for the 8-way
  //   or gate. 
  //   OR 1a
  //   or 1b
  //   or 1c
  //   or 1d
  //   or 2a
  //   or 2b
  //   or 3
  //   3
endmodule
