// Logisim project Assignment2.circ as structural Verilog: 19 circuits, main circuit Mux4Way16
module Not (
  input  in,
  output out
);

  nand nand_1 (out, in, in);

  // Notes on the sheet:
  //   Use only a built-in Nand gate for this (found in Gates>NAND).
  //   Once you are done go to Simulate>Test Vector.
  //   Select the Not.txt file, and run it to try the test cases
endmodule

module And (
  input  a,
  input  b,
  output out
);

  wire nand_1_out;

  nand nand_1 (nand_1_out, a, b);
  nand nand_2 (out, nand_1_out, nand_1_out);

  // Notes on the sheet:
  //   Simple Gate Implementation using Nand and Not
  //   For all gates in this assignment (except Nand),you are required to use
  //   the custom subcircuits you build, rather than the built-in gates.
  //   NAND Gate 1
  //   NAND Gate 2
endmodule

module Or (
  input  a,
  input  b,
  output out
);

  wire nand_1_out, nand_2_out;

  nand nand_1 (nand_1_out, a, a);
  nand nand_2 (nand_2_out, b, b);
  nand nand_3 (out, nand_1_out, nand_2_out);

  // Notes on the sheet:
  //   This function can be defined in terms of boolean expressions previously implemented
  //   It helps to start by looking at the expression as Not(Not(A Or B)) and using boolean
  //   algebra to transform this into something we can implement
  //   A NAND
  //   B NAND
  //   AB NAND
endmodule

module Xor (
  input  a,
  input  b,
  output out
);

  wire b__1a_out, nand_1_out, nand_2_out, nand_3_out;

  nand nand_1 (nand_1_out, a, a);
  nand nand_2 (nand_2_out, b, b);
  nand nand_3 (nand_3_out, a, nand_2_out);
  nand b__1a (b__1a_out, nand_1_out, b);
  nand _2a__2b (out, nand_3_out, b__1a_out);

  // Notes on the sheet:
  //   This function can also be defined in terms of boolean expressions already created. 
  //   Try to express what the Xor gate does in english, then translate that to a boolean
  //   expression that you can implement!
  //   a,a
  //   NAND 1a
  //   b,b
  //   NAND 1b
  //   a, 1b
  //   nand 2a
  //   NAND 2b
  //   NAND 3
  //   the XOR gate is similar to the OR gate, but its different in that it has to be
  //   one or the other it can't be both A and B
endmodule

module Mux (
  input  sel,
  input  a,
  input  b,
  output out
);

  wire B__sel_out, nand_1_out, sel_sel_out;

  nand B__sel (B__sel_out, sel, b);
  nand nand_1 (nand_1_out, sel_sel_out, a);
  nand sel_sel (sel_sel_out, sel, sel);
  nand t__u (out, nand_1_out, B__sel_out);

  // Notes on the sheet:
  //   Function:
  //   If sel == 0, out = a;
  //   	else out = b;
  //   Can be implemented with And, or and Not. Try a truth table!
  //   NAND u
  //   NAND t
  //   NAND n
  //   NAND v
endmodule

module DMux (
  input  sel,
  input  in,
  output a,
  output b
);

  wire in___t_out, in__s_out, sel_sel_out;

  nand in___t (in___t_out, sel_sel_out, in);
  nand u_u (a, in___t_out, in___t_out);
  nand sel_sel (sel_sel_out, sel, sel);
  nand in__s (in__s_out, sel, in);
  nand v_v (b, in__s_out, in__s_out);

  // Notes on the sheet:
  //   Function:
  //   If sel == 0, [a, b] = [in, 0]
  //   	else, [a, b] = [0, in]
  //   Same as before, use a truth table and basic logic gates.
  //   nand u
  //   nand w
  //   nand t
  //   nand v
  //   nand x
endmodule

module Not16 (
  input  [15:0] in,
  output [15:0] out
);

  nand nand_1 (out[0], in[0], in[0]);
  nand nand_2 (out[1], in[1], in[1]);
  nand nand_3 (out[2], in[2], in[2]);
  nand nand_4 (out[3], in[3], in[3]);
  nand nand_5 (out[4], in[4], in[4]);
  nand nand_6 (out[5], in[5], in[5]);
  nand nand_7 (out[6], in[6], in[6]);
  nand nand_8 (out[7], in[7], in[7]);
  nand nand_9 (out[8], in[8], in[8]);
  nand nand_10 (out[9], in[9], in[9]);
  nand nand_11 (out[10], in[10], in[10]);
  nand nand_12 (out[11], in[11], in[11]);
  nand nand_13 (out[12], in[12], in[12]);
  nand nand_14 (out[13], in[13], in[13]);
  nand nand_15 (out[14], in[14], in[14]);
  nand nand_16 (out[15], in[15], in[15]);

  // Notes on the sheet:
  //   Function:
  //   For all i from 0 .. 15, out[i] = Not(in[i])
  //   These are rather repetitive, you will use the splitter element (shown below)
  //   a lot. You already have an elementary version of each of these gates, the implementation
  //   of a 16-bit gate is just a matter of constructing an array of n elementary gates, where
  //   each gate operates separately on each bit.
  //   Changing the spacing attribute on the splitter can help a lot for these
endmodule

module And16 (
  input  [15:0] a,
  input  [15:0] b,
  output [15:0] out
);

  wire [15:0] nand_1_out;

  assign nand_1_out = ~(a & b);  // NAND_Gate nand_1, 16 bits wide
  Not16 not16_1 (.in(nand_1_out), .out(out));

  // Notes on the sheet:
  //   Function:
  //   For all i from 0 .. 15, out[i] = And(in[i])
  //   Reuse the not16 gate i made
endmodule

module Or16 (
  input  [15:0] a,
  input  [15:0] b,
  output [15:0] out
);

  wire [15:0] not16_1_out, not16_2_out;

  Not16 not16_1 (.in(a), .out(not16_1_out));
  Not16 not16_2 (.in(b), .out(not16_2_out));
  assign out = ~(not16_1_out & not16_2_out);  // NAND_Gate A_B, 16 bits wide

  // Notes on the sheet:
  //   Function:
  //   For all i from 0 .. 15, out[i] = Or(in[i])
  //   not16 A
  //   not16 B
  //   nand C
endmodule

module Mux16 (
  input  sel,
  input  [15:0] a,
  input  [15:0] b,
  output [15:0] out
);

  wire [15:0] and16_1_out, and16_2_out, not16_1_out;

  And16 and16_1 (.a(not16_1_out), .b(a), .out(and16_1_out));
  And16 and16_2 (.a({16{sel}}), .b(b), .out(and16_2_out));
  Not16 not16_1 (.in({16{sel}}), .out(not16_1_out));
  Or16 or16_1 (.a(and16_1_out), .b(and16_2_out), .out(out));

  // Notes on the sheet:
  //   Function:
  //   If sel == 0, out = a
  //   	else, out = b
  //   An n-bit multiplexer is just the result of feeding the same selection bit
  //   into n 1-bit multiplexers. Again, splitters and lots of the elementary version
  //   of the gate.
endmodule

module Or8Way (
  input  [7:0] in,
  output out
);

  wire _1a_1b_out, _1c_1d_out, in_0__in_1_out, in_2__in_3_out, in_4__in_5_out, in_6__in_7_out;

  Or in_0__in_1 (.a(in[0]), .b(in[1]), .out(in_0__in_1_out));
  Or in_2__in_3 (.a(in[2]), .b(in[3]), .out(in_2__in_3_out));
  Or in_4__in_5 (.a(in[4]), .b(in[5]), .out(in_4__in_5_out));
  Or in_6__in_7 (.a(in[6]), .b(in[7]), .out(in_6__in_7_out));
  Or _1a_1b (.a(in_0__in_1_out), .b(in_2__in_3_out), .out(_1a_1b_out));
  Or _1c_1d (.a(in_4__in_5_out), .b(in_6__in_7_out), .out(_1c_1d_out));
  Or _2a_2b (.a(_1a_1b_out), .b(_1c_1d_out), .out(out));

  // Notes on the sheet:
  //   Function:
  //   Out = in[0] Or in[1] Or ... Or in[7]
  //   Think forks for this one
  //   Try to get a 3-way Or gate first, then use the same process for the 8-way
  //   or gate. 
  //   OR 1a
  //   or 1b
  //   or 1c
  //   or 1d
  //   or 2a
  //   or 2b
  //   or 3
  //   3
endmodule

module Mux4Way16 (
  input  [1:0] sel,
  input  [15:0] a,
  input  [15:0] b,
  input  [15:0] c,
  input  [15:0] d,
  output [15:0] out1
);

  wire [15:0] mux16_1_out, mux16_2_out;

  Multiplexer #(.enable("false")) multiplexer_1 ();  // open: in0, in1, out, sel
  Mux16 mux16_1 (.sel(sel[0]), .a(a), .b(b), .out(mux16_1_out));
  Mux16 mux16_2 (.sel(sel[0]), .a(c), .b(d), .out(mux16_2_out));
  Mux16 mux16_3 (.sel(sel[1]), .a(mux16_1_out), .b(mux16_2_out), .out(out1));

  // Notes on the sheet:
  //   Play around with it to understand how this gate works
  //   You are free to use this as long as it remains the 16-bit 2-way multiplexer
  //   I will be using the logic gates I created in assignment 1
endmodule

module Mux8Way16 (
  input  [2:0] sel,
  input  [15:0] a,
  input  [15:0] b,
  input  [15:0] c,
  input  [15:0] d,
  input  [15:0] e,
  input  [15:0] f,
  input  [15:0] g,
  input  [15:0] h,
  output [15:0] out1
);

  wire [15:0] mux16_1_out, mux16_2_out, mux16_3_out, mux16_4_out, mux16_5_out, mux16_6_out;

  Mux16 mux16_1 (.sel(sel[0]), .a(a), .b(b), .out(mux16_1_out));
  Mux16 mux16_2 (.sel(sel[0]), .a(c), .b(d), .out(mux16_2_out));
  Mux16 mux16_3 (.sel(sel[0]), .a(e), .b(f), .out(mux16_3_out));
  Mux16 mux16_4 (.sel(sel[0]), .a(g), .b(h), .out(mux16_4_out));
  Mux16 mux16_5 (.sel(sel[1]), .a(mux16_3_out), .b(mux16_4_out), .out(mux16_5_out));
  Mux16 mux16_6 (.sel(sel[1]), .a(mux16_1_out), .b(mux16_2_out), .out(mux16_6_out));
  Mux16 mux16_7 (.sel(sel[2]), .a(mux16_6_out), .b(mux16_5_out), .out(out1));
endmodule

module DMux4Way (
  input  [1:0] sel,
  input  in1,
  output a,
  output b,
  output c,
  output d
);

  wire in__sel_1_a, in__sel_1_b;

  DMux in__sel_1 (.sel(sel[1]), .in(in1), .a(in__sel_1_a), .b(in__sel_1_b));
  DMux Aa__sel_0 (.sel(sel[0]), .in(in__sel_1_a), .a(a), .b(b));
  DMux Ab__sel_0 (.sel(sel[0]), .in(in__sel_1_b), .a(c), .b(d));

  // Notes on the sheet:
  //   You are free to use this as long as you don't change the settings
  //   Play around with it to understand how this gate works
  //   I will be using what I created in assignment 1 because I think it is more fun that way
  //   Dmux A
  //   Dmux B
  //   Dmux C
endmodule

module DMux8Way (
  input  [2:0] sel,
  input  in1,
  output a,
  output b,
  output c,
  output d,
  output e,
  output f,
  output g,
  output h
);

  wire Aa__sel_1_a, Aa__sel_1_b, Ab__sel_1_a, Ab__sel_1_b, in__sel_2_a, in__sel_2_b;

  DMux in__sel_2 (.sel(sel[2]), .in(in1), .a(in__sel_2_a), .b(in__sel_2_b));
  DMux Aa__sel_1 (.sel(sel[1]), .in(in__sel_2_a), .a(Aa__sel_1_a), .b(Aa__sel_1_b));
  DMux Ab__sel_1 (.sel(sel[1]), .in(in__sel_2_b), .a(Ab__sel_1_a), .b(Ab__sel_1_b));
  DMux Ba__sel_0 (.sel(sel[0]), .in(Aa__sel_1_a), .a(a), .b(b));
  DMux dmux_1 (.sel(sel[0]), .in(Aa__sel_1_b), .a(c), .b(d));
  DMux dmux_2 (.sel(sel[0]), .in(Ab__sel_1_a), .a(e), .b(f));
  DMux Cb__sel_0 (.sel(sel[0]), .in(Ab__sel_1_b), .a(g), .b(h));

  // Notes on the sheet:
  //   DmuxA
  //   Dmux B
  //   Dmux C
  //   Dmux D
  //   DMux E
  //   Dmux F
  //   Dmux G
endmodule

module HalfAdder (
  input  a,
  input  b,
  output sum,
  output car
);

  Xor xor_1 (.a(a), .b(b), .out(sum));
  And and_1 (.a(a), .b(b), .out(car));
endmodule

module FullAdder (
  input  a,
  input  b,
  input  c,
  output sum,
  output carry
);

  wire a_b_car, a_b_sum, A_sum___c_car;

  HalfAdder a_b (.a(a), .b(b), .sum(a_b_sum), .car(a_b_car));
  HalfAdder A_sum___c (.a(a_b_sum), .b(c), .sum(sum), .car(A_sum___c_car));
  Or A_car___B_car (.a(A_sum___c_car), .b(a_b_car), .out(carry));

  // Notes on the sheet:
  //   HA-A
  //   HA-B
  //   OR-C
endmodule

module Add16 (
  input  [15:0] a,
  input  [15:0] b,
  output [15:0] out1
);

  wire fulladder_1_carry, fulladder_2_carry, fulladder_3_carry, fulladder_4_carry, fulladder_5_carry,
       fulladder_6_carry, fulladder_7_carry, fulladder_8_carry, fulladder_9_carry, fulladder_10_carry,
       fulladder_11_carry, fulladder_12_carry, fulladder_13_carry, fulladder_14_carry, fulladder_15_carry;

  FullAdder fulladder_1 (.a(a[0]), .b(b[0]), .c(1'b0), .sum(out1[0]), .carry(fulladder_1_carry));
  FullAdder fulladder_2 (.a(a[1]), .b(b[1]), .c(fulladder_1_carry), .sum(out1[1]), .carry(fulladder_2_carry));
  FullAdder fulladder_3 (.a(a[2]), .b(b[2]), .c(fulladder_2_carry), .sum(out1[2]), .carry(fulladder_3_carry));
  FullAdder fulladder_4 (.a(a[3]), .b(b[3]), .c(fulladder_3_carry), .sum(out1[3]), .carry(fulladder_4_carry));
  FullAdder fulladder_5 (.a(a[4]), .b(b[4]), .c(fulladder_4_carry), .sum(out1[4]), .carry(fulladder_5_carry));
  FullAdder fulladder_6 (.a(a[5]), .b(b[5]), .c(fulladder_5_carry), .sum(out1[5]), .carry(fulladder_6_carry));
  FullAdder fulladder_7 (.a(a[6]), .b(b[6]), .c(fulladder_6_carry), .sum(out1[6]), .carry(fulladder_7_carry));
  FullAdder fulladder_8 (.a(a[7]), .b(b[7]), .c(fulladder_7_carry), .sum(out1[7]), .carry(fulladder_8_carry));
  FullAdder fulladder_9 (.a(a[8]), .b(b[8]), .c(fulladder_8_carry), .sum(out1[8]), .carry(fulladder_9_carry));
  FullAdder fulladder_10 (.a(a[9]), .b(b[9]), .c(fulladder_9_carry), .sum(out1[9]), .carry(fulladder_10_carry));
  FullAdder fulladder_11 (.a(a[10]), .b(b[10]), .c(fulladder_10_carry), .sum(out1[10]), .carry(fulladder_11_carry));
  FullAdder fulladder_12 (.a(a[11]), .b(b[11]), .c(fulladder_11_carry), .sum(out1[11]), .carry(fulladder_12_carry));
  FullAdder fulladder_13 (.a(a[12]), .b(b[12]), .c(fulladder_12_carry), .sum(out1[12]), .carry(fulladder_13_carry));
  FullAdder fulladder_14 (.a(a[13]), .b(b[13]), .c(fulladder_13_carry), .sum(out1[13]), .carry(fulladder_14_carry));
  FullAdder fulladder_15 (.a(a[14]), .b(b[14]), .c(fulladder_14_carry), .sum(out1[14]), .carry(fulladder_15_carry));
  FullAdder fulladder_16 (.a(a[15]), .b(b[15]), .c(fulladder_15_carry), .sum(out1[15]));  // open: carry

  // Notes on the sheet:
  //   FA-A
  //   FA-B
  //   FA-C
  //   FA-D
  //   FA-E
  //   FA-F
  //   FA-G
  //   FA-H
  //   FA-I
  //   FA-J
  //   FA-K
  //   FA-L
  //   FA-M
  //   FA-N
  //   FN-O
  //   FN-P
endmodule

module Inc16 (
  input  [15:0] in1,
  output [15:0] out1
);

  Add16 add16_1 (.a(in1), .b(16'h1), .out1(out1));
endmodule
