// Logisim project Assignment4_b.circ as structural Verilog: 4 circuits, main circuit RAM512
module RAM64 (
  input  [5:0] address,
  input  load,
  input  [15:0] in,
  output [15:0] out
);

  wire clock_1_out;

  RAM #(.addrWidth(6), .dataWidth(16)) ram_1 (
    .addr(address), .we(load), .clk(clock_1_out), .din(in), .dout(out));  // open: oe
  Clock clock_1 (.out(clock_1_out));

  // Notes on the sheet:
  //   With the recursive approach for building RAM, there are too many gates for the simulator, and this leads to performance
  //   issues. For this reason, we have separated the assignment into two halves. This subcircuit is already completed and uses
  //   the built-in RAM module.
  //   RAM64 x 64 means that the address space has 64 registers, each containing 16 bits. Write-Enable is the same
  //   as the Load Input. C3 is for a clock input (you will need to connect a clock). The rightmost port is the output
  //   data, the upper left port is the address and the bottom left port is the incoming data.
  //   You will use the built-in RAM for a future assignment. I recommend playing around with it!
endmodule

module RAM512 (
  input  load,
  input  [8:0] address,
  input  [15:0] in,
  output [15:0] out
);

  wire and_1_out, and_2_out, and_3_out, and_4_out, and_5_out, and_6_out, and_7_out, and_8_out,
       decoder_1_out0, decoder_1_out1, decoder_1_out2, decoder_1_out3, decoder_1_out4, decoder_1_out5,
       decoder_1_out6, decoder_1_out7;
  wire [15:0] ram64_1_out, ram64_2_out, ram64_3_out, ram64_4_out, ram64_5_out, ram64_6_out, ram64_7_out,
       ram64_8_out;

  Decoder #(.select(3)) decoder_1 (
    .out0(decoder_1_out0), .out1(decoder_1_out1), .out2(decoder_1_out2), .out3(decoder_1_out3),
    .out4(decoder_1_out4), .out5(decoder_1_out5), .out6(decoder_1_out6), .out7(decoder_1_out7),
    .sel(address[8:6]));  // open: en
  and and_1 (and_1_out, load, decoder_1_out0);
  and and_2 (and_2_out, load, decoder_1_out1);
  and and_3 (and_3_out, load, decoder_1_out2);
  and and_4 (and_4_out, load, decoder_1_out3);
  and and_5 (and_5_out, load, decoder_1_out4);
  and and_6 (and_6_out, load, decoder_1_out5);
  and and_7 (and_7_out, load, decoder_1_out6);
  and and_8 (and_8_out, load, decoder_1_out7);
  RAM64 ram64_1 (.address(address[5:0]), .load(and_1_out), .in(in), .out(ram64_1_out));
  RAM64 ram64_2 (.address(address[5:0]), .load(and_2_out), .in(in), .out(ram64_2_out));
  RAM64 ram64_3 (.address(address[5:0]), .load(and_3_out), .in(in), .out(ram64_3_out));
  RAM64 ram64_4 (.address(address[5:0]), .load(and_4_out), .in(in), .out(ram64_4_out));
  RAM64 ram64_5 (.address(address[5:0]), .load(and_5_out), .in(in), .out(ram64_5_out));
  RAM64 ram64_6 (.address(address[5:0]), .load(and_6_out), .in(in), .out(ram64_6_out));
  RAM64 ram64_7 (.address(address[5:0]), .load(and_7_out), .in(in), .out(ram64_7_out));
  RAM64 ram64_8 (.address(address[5:0]), .load(and_8_out), .in(in), .out(ram64_8_out));
  Multiplexer #(.enable("false"), .select(3), .width(16)) multiplexer_1 (
    .in0(ram64_1_out), .in1(ram64_2_out), .in2(ram64_3_out), .in3(ram64_4_out), .in4(ram64_5_out),
    .in5(ram64_6_out), .in6(ram64_7_out), .in7(ram64_8_out), .out(out), .sel(address[8:6]));

  // Notes on the sheet:
  //   RAM512 can be built out of multiple RAM64 chips in a similar fashion to how
  //   RAM64 was constructed.
endmodule

module RAM4K (
  input  load,
  input  [11:0] address,
  input  [15:0] in,
  output [15:0] out
);

  wire and_1_out, and_2_out, and_3_out, and_4_out, and_5_out, and_6_out, and_7_out, and_8_out,
       decoder_1_out0, decoder_1_out1, decoder_1_out2, decoder_1_out3, decoder_1_out4, decoder_1_out5,
       decoder_1_out6, decoder_1_out7;
  wire [15:0] ram512_1_out, ram512_2_out, ram512_3_out, ram512_4_out, ram512_5_out, ram512_6_out,
       ram512_7_out, ram512_8_out;

  Decoder #(.select(3)) decoder_1 (
    .out0(decoder_1_out0), .out1(decoder_1_out1), .out2(decoder_1_out2), .out3(decoder_1_out3),
    .out4(decoder_1_out4), .out5(decoder_1_out5), .out6(decoder_1_out6), .out7(decoder_1_out7),
    .sel(address[11:9]));  // open: en
  and and_1 (and_1_out, load, decoder_1_out0);
  and and_2 (and_2_out, load, decoder_1_out1);
  and and_3 (and_3_out, load, decoder_1_out2);
  and and_4 (and_4_out, load, decoder_1_out3);
  and and_5 (and_5_out, load, decoder_1_out4);
  and and_6 (and_6_out, load, decoder_1_out5);
  and and_7 (and_7_out, load, decoder_1_out6);
  and and_8 (and_8_out, load, decoder_1_out7);
  RAM512 ram512_1 (.load(and_1_out), .address(address[8:0]), .in(in), .out(ram512_1_out));
  RAM512 ram512_2 (.load(and_2_out), .address(address[8:0]), .in(in), .out(ram512_2_out));
  RAM512 ram512_3 (.load(and_3_out), .address(address[8:0]), .in(in), .out(ram512_3_out));
  RAM512 ram512_4 (.load(and_4_out), .address(address[8:0]), .in(in), .out(ram512_4_out));
  RAM512 ram512_5 (.load(and_5_out), .address(address[8:0]), .in(in), .out(ram512_5_out));
  RAM512 ram512_6 (.load(and_6_out), .address(address[8:0]), .in(in), .out(ram512_6_out));
  RAM512 ram512_7 (.load(and_7_out), .address(address[8:0]), .in(in), .out(ram512_7_out));
  RAM512 ram512_8 (.load(and_8_out), .address(address[8:0]), .in(in), .out(ram512_8_out));
  Multiplexer #(.enable("false"), .select(3), .width(16)) multiplexer_1 (
    .in0(ram512_1_out), .in1(ram512_2_out), .in2(ram512_3_out), .in3(ram512_4_out), .in4(ram512_5_out),
    .in5(ram512_6_out), .in6(ram512_7_out), .in7(ram512_8_out), .out(out), .sel(address[11:9]));

  // Notes on the sheet:
  //   Use the previously implemented RAM512 chip for this chip
endmodule

module RAM16K (
  input  load,
  input  [13:0] address,
  input  [15:0] in,
  output [15:0] out
);

  wire and_1_out, and_2_out, and_3_out, and_4_out, decoder_1_out0, decoder_1_out1, decoder_1_out2,
       decoder_1_out3;
  wire [15:0] ram4k_1_out, ram4k_2_out, ram4k_3_out, ram4k_4_out;

  Decoder #(.select(2)) decoder_1 (
    .out0(decoder_1_out0), .out1(decoder_1_out1), .out2(decoder_1_out2), .out3(decoder_1_out3),
    .sel(address[13:12]));  // open: en
  and and_1 (and_1_out, load, decoder_1_out0);
  and and_2 (and_2_out, load, decoder_1_out1);
  and and_3 (and_3_out, load, decoder_1_out2);
  and and_4 (and_4_out, load, decoder_1_out3);
  RAM4K ram4k_1 (.load(and_1_out), .address(address[11:0]), .in(in), .out(ram4k_1_out));
  RAM4K ram4k_2 (.load(and_2_out), .address(address[11:0]), .in(in), .out(ram4k_2_out));
  RAM4K ram4k_3 (.load(and_3_out), .address(address[11:0]), .in(in), .out(ram4k_3_out));
  RAM4K ram4k_4 (.load(and_4_out), .address(address[11:0]), .in(in), .out(ram4k_4_out));
  Multiplexer #(.enable("false"), .select(2), .width(16)) multiplexer_1 (
    .in0(ram4k_1_out), .in1(ram4k_2_out), .in2(ram4k_3_out), .in3(ram4k_4_out), .out(out),
    .sel(address[13:12]));

  // Notes on the sheet:
  //   Use the previously implemented RAM4K for this chip.
endmodule
